// Logisim project gorbit-ram.circ as structural Verilog: 3 circuits, main circuit main
module main (
  input  in_1,
  input  in_2
);

  wire aluop, and_1_out, and_2_out, branch, charrdy, clock_1_out, clock_2_out, clock_3_out, clock_4_out,
       clock_5_out, clock_6_out, clock_7_out, clock_8_out, incrpc, loadir, loadmem, loadpc, loadptr, loadx,
       nextchar, putchar;
  wire [1:0] dsel;
  wire [6:0] bit_extender_1_out, keyboard_1_data;
  wire [7:0] ALU_out, bit_extender_2_out, multiplexer_1_out, multiplexer_2_out, multiplexer_3_out,
       multiplexer_4_out, PC_q, PTR_q, ram_1_data, shifter_1_out, X_q;

  Shifter shifter_1 (.in(ram_1_data), .\dist (3'b001), .out(shifter_1_out));
  Counter #(.ongoal("stay")) PC (
    .load(loadpc), .D(shifter_1_out), .count(incrpc), .Q(PC_q), .clk(clock_1_out));  // open: carry, clr
  Clock clock_1 (.out(clock_1_out));
  Register PTR (.D(ram_1_data), .en(loadptr), .Q(PTR_q), .clk(clock_2_out));  // open: clr
  Clock clock_2 (.out(clock_2_out));
  Bit_Extender #(.out_width(7)) bit_extender_1 (.in(multiplexer_1_out), .out(bit_extender_1_out));
  Multiplexer #(.select(2), .width(8), .enable("false")) multiplexer_1 (
    .in0(ram_1_data), .in3(X_q), .out(multiplexer_1_out), .sel(dsel));  // open: in1, in2
  Multiplexer #(.select(2), .width(8), .enable("false")) multiplexer_2 (
    .in0(PC_q), .in1(PTR_q), .out(multiplexer_2_out), .sel(dsel));  // open: in2, in3
  Multiplexer #(.select(2), .width(8), .enable("false")) multiplexer_3 (
    .in1(bit_extender_2_out), .in2(ALU_out), .in3(X_q), .out(multiplexer_3_out), .sel(dsel));  // open: in0
  TTY tty_1 (.data(bit_extender_1_out), .clk(clock_3_out), .we(putchar));  // open: clr
  Clock clock_3 (.out(clock_3_out));
  Clock clock_4 (.out(clock_4_out));
  Keyboard keyboard_1 (.clk(clock_4_out), .re(nextchar), .avail(charrdy), .data(keyboard_1_data));  // open: clr
  Clock clock_5 (.out(clock_5_out));
  RAM #(.bus("separate")) ram_1 (
    .addr(multiplexer_2_out), .din(multiplexer_3_out), .data(ram_1_data), .str(loadmem), .clk(clock_5_out),
    .ld(1'b1));  // open: sel, clr
  assign bit_extender_2_out = {{1{1'b0}}, keyboard_1_data};  // Bit_Extender bit_extender_2
  Register IR (.D(ram_1_data), .en(loadir), .clk(clock_6_out));  // open: Q, clr
  Clock clock_6 (.out(clock_6_out));
  Multiplexer #(.select(2), .width(8), .enable("false")) multiplexer_4 (
    .in0(ram_1_data), .in1(bit_extender_2_out), .in2(ALU_out), .out(multiplexer_4_out), .sel(dsel));  // open: in3
  Clock clock_7 (.out(clock_7_out));
  Clock clock_8 (.out(clock_8_out));
  Register X (.D(multiplexer_4_out), .en(loadx), .Q(X_q), .clk(clock_7_out));  // open: clr
  and and_1 (and_1_out, in_2, ~in_1);  // AND_Gate
  alu ALU (.A(X_q), .B(ram_1_data), .op(aluop), .branch(branch), .out(ALU_out));
  and and_2 (and_2_out, clock_8_out, and_1_out);
endmodule

module alu (
  input  [7:0] A,
  input  [7:0] B,
  input  op,
  output branch,
  output [7:0] out
);

  wire [7:0] adder_1_out, xor_1_out;

  Adder adder_1 (.a(A), .b(B), .out(adder_1_out));  // open: cin, cout
  assign xor_1_out = B ^ A;  // XOR_Gate xor_1, 8 bits wide
  Multiplexer #(.width(8), .enable("false")) multiplexer_1 (.in0(adder_1_out), .in1(xor_1_out), .out(out), .sel(op));
  nor nor_1 (branch, A[0], A[1], A[2], A[3], A[4], A[5], A[6], A[7]);
endmodule

module con (
  input  branch,
  input  [3:0] instruction
);

  Counter #(.width(3), .max('h7)) T_State ();  // open: load, D, count, Q, carry, clk, clr
  ROM rom_1 ();  // open: addr, data, sel
endmodule
